// Logisim project Dragon_5.circ as structural Verilog: 5 circuits, main circuit main
module main (
);

  Pipeline_ID ID_Stage ();  // open: Inst_Cache_1_IN, Inst_Cache_2_IN, WE, Inst_1_out, Inst_2_out
  Register_File reg_file ();  // open: RegF_rst, RegF_WE, RegF_A1, RegF_A2, RegF_A3, RegF_WD, RegF_D1, RegF_D2
  ALU Arithmetic_logic_Unit ();  // open: ALU_OP_IN, ALU_A_IN, ALU_B_IN, ALU_FLAG_IN, ALU_RES_OUT, ALU_FLAG_OUT
endmodule

module ALU (
  input  [3:0] ALU_OP_IN,
  input  [15:0] ALU_A_IN,
  input  [15:0] ALU_B_IN,
  input  [15:0] ALU_FLAG_IN,
  output [15:0] ALU_RES_OUT,
  output [15:0] ALU_FLAG_OUT
);

  wire adder_1_cout, adder_2_cout, adder_3_cout;
  wire [15:0] adder_1_out;

  Pull_Resistor pull_resistor_1 (.node(ALU_RES_OUT));
  Adder #(.width(4)) adder_1 (
    .a(ALU_A_IN[3:0]), .b(ALU_B_IN[3:0]), .out(adder_1_out[3:0]), .cout(adder_1_cout));  // open: cin
  Adder #(.width(4)) adder_2 (
    .a(ALU_A_IN[7:4]), .b(ALU_B_IN[7:4]), .out(adder_1_out[7:4]), .cin(adder_1_cout), .cout(adder_2_cout));
  Adder #(.width(4)) adder_3 (
    .a(ALU_A_IN[11:8]), .b(ALU_B_IN[11:8]), .out(adder_1_out[11:8]), .cin(adder_2_cout), .cout(adder_3_cout));
  Adder #(.width(4)) adder_4 (
    .a(ALU_A_IN[15:12]), .b(ALU_B_IN[15:12]), .out(adder_1_out[15:12]), .cin(adder_3_cout));  // open: cout
  Controlled_Buffer #(.width(16)) controlled_buffer_1 (.in(adder_1_out));  // open: out, en

  // Other names for the same wires on the sheet: ALU_A[15:0] = ALU_A_IN; ALU_B[15:0] = ALU_B_IN;
  //   ALU_OP[3:0] = ALU_OP_IN; ALU_RES[15:0] = ALU_RES_OUT
endmodule

module Register_File (
  input  RegF_rst,
  input  RegF_WE,
  input  [4:0] RegF_A1,
  input  [4:0] RegF_A2,
  input  [4:0] RegF_A3,
  input  [15:0] RegF_WD,
  output [15:0] RegF_D1,
  output [15:0] RegF_D2
);

  wire clock_1_out;
  wire [4:0] multiplexer_1_out, multiplexer_2_out;
  wire [15:0] bit_extender_1_out, bit_extender_2_out;

  assign bit_extender_1_out = {{11{1'b0}}, multiplexer_1_out};  // Bit_Extender bit_extender_1
  Multiplexer #(.width(5)) multiplexer_1 (.in0(RegF_A1), .in1(RegF_A3), .out(multiplexer_1_out), .sel(RegF_WE));
  Clock clock_1 (.out(clock_1_out));
  assign bit_extender_2_out = {{11{1'b0}}, multiplexer_2_out};  // Bit_Extender bit_extender_2
  Multiplexer #(.width(5)) multiplexer_2 (.in0(RegF_A2), .in1(RegF_A3), .out(multiplexer_2_out), .sel(RegF_WE));
  RAM #(.addrWidth(16), .dataWidth(16)) ram_1 (
    .addr(bit_extender_1_out), .we(RegF_WE), .oe(1'b1), .clk(clock_1_out), .din(RegF_WD), .dout(RegF_D1));
  RAM #(.addrWidth(16), .dataWidth(16)) ram_2 (
    .addr(bit_extender_2_out), .we(RegF_WE), .oe(1'b1), .clk(clock_1_out), .din(RegF_WD), .dout(RegF_D2));

  // Other names for the same wires on the sheet: RegF_bus_A[15:0] = RegF_D1; RegF_bus_B[15:0] = RegF_D2;
  //   RegF_D_in[15:0] = RegF_WD; RegF_reset = RegF_rst
endmodule

module Pipeline_ID (
  input  WE,
  input  [15:0] Inst_Cache_1_IN,
  input  [15:0] Inst_Cache_2_IN,
  output [15:0] Inst_1_out,
  output [15:0] Inst_2_out
);

  wire reset, undriven;

  Register #(.width(16)) register_1 (.D(Inst_Cache_1_IN), .en(undriven), .clk(WE), .Q(Inst_1_out), .clr(reset));
  Clock clock_1 (.out(WE));
  Register #(.width(16)) register_2 (.D(Inst_Cache_2_IN), .en(undriven), .clk(WE), .Q(Inst_2_out), .clr(reset));
endmodule

module Instruction_Cache (
  input  [15:0] InstC_A,
  input  [3:0] InstC_MBR,
  input  InstC_WE,
  input  InstC_HDU_Perm,
  output [19:0] InstC_RAM_A_BUS,
  output InstC_CU_STALL_Issue
);

  wire and_1_out, and_2_out, clock_1_out, clock_2_out, clock_3_out, clock_4_out, clock_5_out, not_1_out,
       not_2_out, not_3_out, or_1_out, or_2_out, or_3_out, or_4_out, undriven, undriven_2, xor_1_out,
       xor_2_out, xor_3_out, xor_4_out;
  wire [7:0] controlled_buffer_2_out, ram_1_dout, ram_2_dout;
  wire [7:7] undriven_3;
  wire [9:0] counter_1_q;
  wire [19:0] adder_1_out, bit_extender_1_out;

  Clock clock_1 (.out(clock_1_out));
  Counter #(.max('h3ff), .width(10)) counter_1 (
    .clr(undriven), .load(1'b0), .up(1'b1), .count(undriven_2), .clk(clock_1_out), .Q(counter_1_q));  // open: D, carry
  and and_1 (and_1_out, InstC_WE, InstC_A[15]);
  not not_1 (not_1_out, and_1_out);
  assign bit_extender_1_out = {{10{counter_1_q[9]}}, counter_1_q};  // Bit_Extender bit_extender_1
  RAM #(.addrWidth(15)) ram_1 (
    .addr(InstC_A[14:0]), .we(and_1_out), .oe(1'b1), .clk(clock_2_out),
    .din({undriven_3[7], 3'b000, InstC_MBR}), .dout(ram_1_dout));
  Clock clock_2 (.out(clock_2_out));
  RAM #(.addrWidth(15)) ram_2 (
    .addr(InstC_A[14:0]), .we(not_1_out), .oe(1'b1), .clk(clock_3_out),
    .din({undriven_3[7], 3'b000, InstC_MBR}), .dout(ram_2_dout));
  Clock clock_3 (.out(clock_3_out));
  Adder #(.width(20)) adder_1 (
    .a(bit_extender_1_out), .b({InstC_MBR, InstC_A[15:1], 1'b0}), .out(adder_1_out));  // open: cin, cout
  assign InstC_RAM_A_BUS = InstC_CU_STALL_Issue ? adder_1_out : 20'bz;  // Controlled_Buffer controlled_buffer_1
  assign controlled_buffer_2_out = InstC_A[15] ? ram_1_dout : 8'bz;  // Controlled_Buffer controlled_buffer_2
  assign controlled_buffer_2_out = not_2_out ? ram_2_dout : 8'bz;  // Controlled_Buffer controlled_buffer_3
  not not_2 (not_2_out, InstC_A[15]);
  Pull_Resistor pull_resistor_1 (.node(controlled_buffer_2_out));
  not not_3 (not_3_out, controlled_buffer_2_out[7]);
  or or_1 (or_1_out, not_3_out, or_4_out);
  and and_2 (and_2_out, InstC_HDU_Perm, or_1_out);
  RAM #(.addrWidth(16), .dataWidth(16)) ram_3 ();  // open: addr, we, oe, clk, din, dout
  xor xor_1 (xor_1_out, controlled_buffer_2_out[3], InstC_MBR[3]);
  xor xor_2 (xor_2_out, controlled_buffer_2_out[2], InstC_MBR[2]);
  xor xor_3 (xor_3_out, controlled_buffer_2_out[1], InstC_MBR[1]);
  xor xor_4 (xor_4_out, controlled_buffer_2_out[0], InstC_MBR[0]);
  or or_2 (or_2_out, xor_1_out, xor_2_out);
  or or_3 (or_3_out, xor_3_out, xor_4_out);
  or or_4 (or_4_out, or_2_out, or_3_out);
  S_R_Flip_Flop s_r_ff_1 (
    .clk(clock_4_out), .Q(InstC_CU_STALL_Issue), .reset(undriven), .preset(and_2_out));  // open: S, R, Qn
  Clock clock_4 (.out(clock_4_out));
  RAM #(.addrWidth(16), .dataWidth(16)) ram_4 (
    .addr(InstC_A), .we(counter_1_q[0]), .oe(1'b1), .clk(clock_5_out));  // open: din, dout
  Clock clock_5 (.out(clock_5_out));

  // Notes on the sheet:
  //   Index
  //   Tag
  //   Valid Bit
  //   1 = Cache Miss
  //   IF CU recieves this signal, gives as control over bus
endmodule
